# Fritzing sketch esp32_sensores_vib_acc (saved by Fritzing 0.9.3b)
circuit board: 6.32231cm x 5.31112cm
breadboards: 2

parts:
  Sensor_Vibración = Vibration sensor module
  Acelerometro = InvenSense MPU6050
  USB = Adafruit Micro USB Breakout [part_number="Adafruit #1833"]
  ESP32_-_Back1 = ESP32 - CAM

nets:
  VCC: Sensor_Vibración.vcc, Acelerometro.VCC, USB.VBUS, ESP32_-_Back1.5V
  GND: Sensor_Vibración.Ground, Acelerometro.GND, USB.GND, ESP32_-_Back1.GND#7
  N1: Sensor_Vibración.Digital_output, ESP32_-_Back1.GPIO12
  N2: Acelerometro.SCL, ESP32_-_Back1.GPIO15
  N3: Acelerometro.SDA, ESP32_-_Back1.GPIO14

notes:
  GY-521
  SW-420
  Conector USB
  ESP32-CAM

custom parts:
  Vibration sensor module: Single-roller type full induction trigger switch. When no vibration or tilt, the product is ON conduction state, and in the steady state, when a vibration or tilt, the switch will be rendered instantly disconnect the conductive resistance increases, generating a current pulse signal, thereby triggering circuit. The default state of the swith is close Digital output Supply voltage:3.3V-5V On-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
  Adafruit Micro USB Breakout: Simple but effective - this breakout board has a USB Micro-B connector, with all 5 pins broken out. Great for pairing with a microcontroller with USB support, or adding USB 5V power to a project. We use a micro-AB connector with through-hole shielding pads for an excellent strong connection - it won't rip off by accident! Comes with one fully assembled and tested micro B breakout PCB and a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
  ESP32 - CAM: The ESP32-CAM has a very competitive small-size camera module that can operate independently as a minimum system with a footprint of only 27*40.5*4.5mm and a deep sleep current of up to 6mA.
